// Logisim project task 1.circ as structural Verilog
module and_gate (
  input  A,
  input  B,
  output OUTPUT
);

  and AND (OUTPUT, A, B);
endmodule

module or_gate (
  input  A,
  input  B,
  output OUTPUT
);

  or OR (OUTPUT, A, B);
endmodule

module not_gate (
  input  A,
  output OUTPUT
);

  not not_1 (OUTPUT, A);

  // Notes on the sheet:
  //   NOT
endmodule

module Nand_gate (
  input  A,
  input  B,
  output OUTPUT
);

  nand NAND (OUTPUT, A, B);
endmodule

module nor_gate (
  input  A,
  input  B,
  output OUTPUT
);

  nor NOR (OUTPUT, A, B);
endmodule

module Xor_gate (
  input  A,
  input  B,
  output OUTPUT
);

  xor XOR (OUTPUT, A, B);
endmodule

module Half_adder (
  input  A,
  input  B,
  output Sum,
  output Carry
);

  xor XOR (Sum, A, B);
  and AND (Carry, A, B);

  // Notes on the sheet:
  //   HALF ADDER CIRCUIT 
endmodule
